# Fritzing sketch ipager (saved by Fritzing 0.9.4)
breadboards: 1

parts:
  Componente3 = Arduino Uno (Rev3) - ICSP
  OLED1 = OLED 128x64 I2C Monochrome Display GND-VDD
  M1 = NRF24L01-BO [package=THT]
  Componente4 = Black Joystick KY-023

nets:
  N1: Componente3.A0, Componente4.VRx
  N2: Componente3.A1, Componente4.VRy
  N3: Componente3.A2, Componente4.SW
  GND: Componente3.GND, OLED1.GND, M1.GND, Componente4.GND
  N4: Componente3.D9_PWM, M1.CE
  N5: Componente3.D10_PWM/SS, M1.CSN
  N6: Componente3.D11_PWM/MOSI, M1.M0
  N7: Componente3.D12/MISO, M1.M1
  N8: Componente3.D13/SCK, M1.SCK
  N9: Componente3.A4/SDA, OLED1.SDA
  N10: Componente3.A5/SCL, OLED1.SCK
  5V: Componente3.5V, OLED1.VDD, M1.VCC, Componente4.+5V

custom parts:
  OLED 128x64 I2C Monochrome Display GND-VDD: OLED 128x64 I2C Monochrome Display. Note: there are two variants of this part, this one is the GND VDD SCK SDA variant. The other is VDD GND SCK SDA. Make sure you select the part that matches your module as using the incorrect part will probably destroy your module! In addition the mounting holes are marked on silkscreen but not by default drilled. If you want drilled mounting holes, copy a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
  NRF24L01-BO: NRF24L01-BO breakout board for the NRF24L01. Pcb view suppressed as unneeded.
  Black Joystick KY-023: Description: The joystick is a combination of 2 analoog potentiometer and a digital switch. Arduino GND --> Module pin - Arduino +5V --> Module pin +5V Arduino Analoog 0 --> Module VRx Arduino Analoog 1 --> Module VRy Arduino Digital --> Module SW Dimensions: 1" x 1.25"
